# Fritzing sketch Untitled Sketch 4 (saved by Fritzing 0.9.3b)
breadboards: 1

parts:
  U1 = NodeMCU V1.0
  S1 = Pushbutton [package="[THT]"]
  R1 = Resistor [tolerance=±5% resistance=220 package=THT]
  Parça1 = LED Tactile Button Breakout v10 [part_number=BOB-10467]  # not connected

nets:
  N1: U1.GND, S1.Pin_3, S1.Pin_4
  N2: U1.D5, R1.Pin_1
  N3: S1.Pin_1, S1.Pin_2, R1.Pin_0

custom parts:
  NodeMCU V1.0: ESP8266 based NodeMCU
